# Fritzing sketch Sequencial (saved by Fritzing 0.9.0b)
breadboards: 1

parts:
  LED1 = LED - 5mm [color="Red (633nm)" package="5 mm [THT]"]
  LED2 = LED - 5mm [color="Red (633nm)" package="5 mm [THT]"]
  LED3 = LED - 5mm [color="Red (633nm)" package="5 mm [THT]"]
  LED4 = LED - 5mm [color="Red (633nm)" package="5 mm [THT]"]
  LED5 = LED - 5mm [color="Red (633nm)" package="5 mm [THT]"]
  LED6 = LED - 5mm [color="Red (633nm)" package="5 mm [THT]"]
  LED7 = LED - 5mm [color="Red (633nm)" package="5 mm [THT]"]
  LED8 = LED - 5mm [color="Red (633nm)" package="5 mm [THT]"]
  LED9 = LED - 5mm [color="Red (633nm)" package="5 mm [THT]"]
  LED10 = LED - 5mm [color="Red (633nm)" package="5 mm [THT]"]
  R1 = Resistor [tolerance=±5% resistance=470 package=THT]
  R2 = Resistor [tolerance=±5% resistance=470 package=THT]
  R3 = Resistor [tolerance=±5% resistance=470 package=THT]
  R4 = Resistor [tolerance=±5% resistance=470 package=THT]
  R5 = Resistor [tolerance=±5% resistance=470 package=THT]
  R6 = Resistor [tolerance=±5% resistance=470 package=THT]
  R7 = Resistor [tolerance=±5% resistance=470 package=THT]
  R8 = Resistor [tolerance=±5% resistance=470 package=THT]
  R9 = Resistor [tolerance=±5% resistance=470 package=THT]
  R10 = Resistor [tolerance=±5% resistance=470 package=THT]
  Componente1 = Arduino Uno (Rev3)
  R11 = Rotary Potentiometer (Small) [maximum_resistance=100kΩ package=THT]
  R12 = Resistor [tolerance=±5% resistance=10k package=THT]
  S1 = Pushbutton [package=THT]
  S2 = Pushbutton [package=THT]
  S3 = Pushbutton [package=THT]
  R13 = Resistor [tolerance=±5% resistance=10k package=THT]
  R14 = Resistor [tolerance=±5% resistance=10k package=THT]

nets:
  N1: LED1.cathode, LED2.cathode, LED3.cathode, LED4.cathode, LED5.cathode, LED6.cathode, LED7.cathode, LED8.cathode, LED9.cathode, LED10.cathode, Componente1.GND, R11.leg2, S1.leg0, S2.leg0, S3.leg0
  N2: LED1.anode, R1.Pin_1
  N3: LED2.anode, R2.Pin_1
  N4: LED3.anode, R3.Pin_1
  N5: LED4.anode, R4.Pin_1
  N6: LED5.anode, R5.Pin_1
  N7: LED6.anode, R6.Pin_1
  N8: LED7.anode, R7.Pin_1
  N9: LED8.anode, R8.Pin_1
  N10: LED9.anode, R9.Pin_1
  N11: LED10.anode, R10.Pin_1
  N12: R1.Pin_0, Componente1.D0/RX
  N13: R2.Pin_0, Componente1.D1/TX
  N14: R3.Pin_0, Componente1.D2
  N15: R4.Pin_0, Componente1.D3_PWM
  N16: R5.Pin_0, Componente1.D4
  N17: R6.Pin_0, Componente1.D5_PWM
  N18: R7.Pin_0, Componente1.D6_PWM
  N19: R8.Pin_0, Componente1.D7
  N20: R9.Pin_0, Componente1.D8
  N21: R10.Pin_0, Componente1.D9_PWM
  N22: Componente1.A0, R11.wiper
  N23: Componente1.D10_PWM/SS, S3.leg1, R13.Pin_1
  N24: Componente1.D11_PWM/MOSI, S2.leg1, R14.Pin_1
  N25: Componente1.D12/MISO, R12.Pin_1, S1.leg1
  N26: Componente1.5V, R11.leg1, R12.Pin_0, R13.Pin_0, R14.Pin_0
